// Logisim project CPU-8bits.circ as structural Verilog: 11 circuits, main circuit SYS-Main
// RAM MAIN
module RAM_Main (
  input  clock,
  input  [3:0] Address,
  input  [7:0] Data,
  input  RW_input
);

  wire not_1_out;
  wire [3:0] AR_q;
  wire [7:0] demultiplexer_1_out0, demultiplexer_1_out1, demultiplexer_1_out2, demultiplexer_1_out3,
       demultiplexer_1_out4, demultiplexer_1_out5, demultiplexer_1_out6, demultiplexer_1_out7,
       demultiplexer_1_out8, demultiplexer_1_out9, demultiplexer_1_out10, demultiplexer_1_out11,
       demultiplexer_1_out12, demultiplexer_1_out13, demultiplexer_1_out14, demultiplexer_1_out15, DR_q,
       multiplexer_1_out, multiplexer_2_out, ram_byte_1_out_3, ram_byte_2_out_3, ram_byte_3_out_3,
       ram_byte_4_out_3, ram_byte_5_out_3, ram_byte_6_out_3, ram_byte_7_out_3, ram_byte_8_out_3,
       ram_byte_9_out_3, ram_byte_10_out_3, ram_byte_11_out_3, ram_byte_12_out_3, ram_byte_13_out_3,
       ram_byte_14_out_3, ram_byte_15_out_3, ram_byte_16_out_3;

  Register #(.width(4), .trigger("high")) AR (.D(Address), .Q(AR_q), .clk(clock));  // open: en, clr
  Multiplexer #(.width(8), .enable("false")) multiplexer_1 (
    .in0(Data), .in1(multiplexer_2_out), .out(multiplexer_1_out), .sel(RW_input));
  Register #(.trigger("high")) DR (.D(multiplexer_1_out), .Q(DR_q), .clk(clock));  // open: en, clr
  Demultiplexer #(.select(4), .width(8), .tristate("true")) demultiplexer_1 (
    .out0(demultiplexer_1_out0), .out1(demultiplexer_1_out1), .out2(demultiplexer_1_out2),
    .out3(demultiplexer_1_out3), .out4(demultiplexer_1_out4), .out5(demultiplexer_1_out5),
    .out6(demultiplexer_1_out6), .out7(demultiplexer_1_out7), .out8(demultiplexer_1_out8),
    .out9(demultiplexer_1_out9), .out10(demultiplexer_1_out10), .out11(demultiplexer_1_out11),
    .out12(demultiplexer_1_out12), .out13(demultiplexer_1_out13), .out14(demultiplexer_1_out14),
    .out15(demultiplexer_1_out15), .in(DR_q), .sel(AR_q), .en(RW_input));
  not not_1 (not_1_out, RW_input);
  RAM_byte ram_byte_1 (.in_2(demultiplexer_1_out0), .in_1(clock), .out_3(ram_byte_1_out_3));
  RAM_byte ram_byte_2 (.in_2(demultiplexer_1_out1), .in_1(clock), .out_3(ram_byte_2_out_3));
  RAM_byte ram_byte_3 (.in_2(demultiplexer_1_out2), .in_1(clock), .out_3(ram_byte_3_out_3));
  Multiplexer #(.select(4), .width(8), .disabled(0)) multiplexer_2 (
    .in0(ram_byte_1_out_3), .in1(ram_byte_2_out_3), .in2(ram_byte_3_out_3), .in3(ram_byte_4_out_3),
    .in4(ram_byte_6_out_3), .in5(ram_byte_5_out_3), .in6(ram_byte_7_out_3), .in7(ram_byte_8_out_3),
    .in8(ram_byte_9_out_3), .in9(ram_byte_11_out_3), .in10(ram_byte_10_out_3), .in11(ram_byte_12_out_3),
    .in12(ram_byte_14_out_3), .in13(ram_byte_13_out_3), .in14(ram_byte_15_out_3), .in15(ram_byte_16_out_3),
    .out(multiplexer_2_out), .sel(AR_q), .en(not_1_out));
  RAM_byte ram_byte_4 (.in_2(demultiplexer_1_out3), .in_1(clock), .out_3(ram_byte_4_out_3));
  RAM_byte ram_byte_5 (.in_2(demultiplexer_1_out5), .in_1(clock), .out_3(ram_byte_5_out_3));
  RAM_byte ram_byte_6 (.in_2(demultiplexer_1_out4), .in_1(clock), .out_3(ram_byte_6_out_3));
  RAM_byte ram_byte_7 (.in_2(demultiplexer_1_out6), .in_1(clock), .out_3(ram_byte_7_out_3));
  RAM_byte ram_byte_8 (.in_2(demultiplexer_1_out7), .in_1(clock), .out_3(ram_byte_8_out_3));
  RAM_byte ram_byte_9 (.in_2(demultiplexer_1_out8), .in_1(clock), .out_3(ram_byte_9_out_3));
  RAM_byte ram_byte_10 (.in_2(demultiplexer_1_out10), .in_1(clock), .out_3(ram_byte_10_out_3));
  RAM_byte ram_byte_11 (.in_2(demultiplexer_1_out9), .in_1(clock), .out_3(ram_byte_11_out_3));
  RAM_byte ram_byte_12 (.in_2(demultiplexer_1_out11), .in_1(clock), .out_3(ram_byte_12_out_3));
  RAM_byte ram_byte_13 (.in_2(demultiplexer_1_out13), .in_1(clock), .out_3(ram_byte_13_out_3));
  RAM_byte ram_byte_14 (.in_2(demultiplexer_1_out12), .in_1(clock), .out_3(ram_byte_14_out_3));
  RAM_byte ram_byte_15 (.in_2(demultiplexer_1_out14), .in_1(clock), .out_3(ram_byte_15_out_3));
  RAM_byte ram_byte_16 (.in_2(demultiplexer_1_out15), .in_1(clock), .out_3(ram_byte_16_out_3));
endmodule

module Generic_4bitRegister (
  input  in_1,
  input  [3:0] in_2,
  output [3:0] out_3
);

  D_Flip_Flop d_ff_1 (.clk(in_1), .D(in_2[0]), .Q(out_3[0]));  // open: Qn, preset, en, reset
  D_Flip_Flop d_ff_2 (.clk(in_1), .D(in_2[1]), .Q(out_3[1]));  // open: Qn, preset, en, reset
  D_Flip_Flop d_ff_3 (.clk(in_1), .D(in_2[2]), .Q(out_3[2]));  // open: Qn, preset, en, reset
  D_Flip_Flop d_ff_4 (.clk(in_1), .D(in_2[3]), .Q(out_3[3]));  // open: Qn, preset, en, reset
endmodule

module Generic_8bitRegister (
  input  in_1,
  input  [7:0] in_2,
  output [7:0] out_3
);

  D_Flip_Flop d_ff_1 (.clk(in_1), .D(in_2[0]), .Q(out_3[0]));  // open: Qn, preset, en, reset
  D_Flip_Flop d_ff_2 (.clk(in_1), .D(in_2[1]), .Q(out_3[1]));  // open: Qn, preset, en, reset
  D_Flip_Flop d_ff_3 (.clk(in_1), .D(in_2[2]), .Q(out_3[2]));  // open: Qn, preset, en, reset
  D_Flip_Flop d_ff_4 (.clk(in_1), .D(in_2[3]), .Q(out_3[3]));  // open: Qn, preset, en, reset
  D_Flip_Flop d_ff_5 (.clk(in_1), .D(in_2[4]), .Q(out_3[4]));  // open: Qn, preset, en, reset
  D_Flip_Flop d_ff_6 (.clk(in_1), .D(in_2[5]), .Q(out_3[5]));  // open: Qn, preset, en, reset
  D_Flip_Flop d_ff_7 (.clk(in_1), .D(in_2[6]), .Q(out_3[6]));  // open: Qn, preset, en, reset
  D_Flip_Flop d_ff_8 (.clk(in_1), .D(in_2[7]), .Q(out_3[7]));  // open: Qn, preset, en, reset
endmodule

module RAM_byte (
  input  in_1,
  input  [7:0] in_2,
  output [7:0] out_3
);

  D_Flip_Flop d_ff_1 (.clk(in_1), .D(in_2[0]), .Q(out_3[0]));  // open: Qn, preset, en, reset
  D_Flip_Flop d_ff_2 (.clk(in_1), .D(in_2[1]), .Q(out_3[1]));  // open: Qn, preset, en, reset
  D_Flip_Flop d_ff_3 (.clk(in_1), .D(in_2[2]), .Q(out_3[2]));  // open: Qn, preset, en, reset
  D_Flip_Flop d_ff_4 (.clk(in_1), .D(in_2[3]), .Q(out_3[3]));  // open: Qn, preset, en, reset
  D_Flip_Flop d_ff_5 (.clk(in_1), .D(in_2[4]), .Q(out_3[4]));  // open: Qn, preset, en, reset
  D_Flip_Flop d_ff_6 (.clk(in_1), .D(in_2[5]), .Q(out_3[5]));  // open: Qn, preset, en, reset
  D_Flip_Flop d_ff_7 (.clk(in_1), .D(in_2[6]), .Q(out_3[6]));  // open: Qn, preset, en, reset
  D_Flip_Flop d_ff_8 (.clk(in_1), .D(in_2[7]), .Q(out_3[7]));  // open: Qn, preset, en, reset
endmodule

// 2
module SYS_Main (
  input  _7,
  input  _8,
  input  _9,
  input  _4,
  input  _5,
  input  _6,
  input  _1,
  input  _2,
  input  _3,
  input  _0
);

  wire Bus_Clock_out, controlled_buffer_1_out, CPU_rw, CPU_stop, ext_displaydriver_1_e0,
       ext_displaydriver_1_e1, ext_displaydriver_1_e2, ext_displaydriver_1_e3, ext_displaydriver_1_e4,
       ext_displaydriver_1_e5, ext_displaydriver_1_e6, ext_displaydriver_2_e0, ext_displaydriver_2_e1,
       ext_displaydriver_2_e2, ext_displaydriver_2_e3, ext_displaydriver_2_e4, ext_displaydriver_2_e5,
       ext_displaydriver_2_e6, not_1_out, On_Off_Switch_q, RW_q;
  wire [7:0] buffer_2_q, Buffer_q, CPU_a_out, CPU_d_out, CPU_display_out, Keypad_Encoder_out_2, ram_1_data;

  assign controlled_buffer_1_out = not_1_out ? Bus_Clock_out : 1'bz;  // Controlled_Buffer controlled_buffer_1
  Clock Bus_Clock (.out(Bus_Clock_out));
  not not_1 (not_1_out, On_Off_Switch_q);
  Register #(.width(1)) On_Off_Switch (
    .D(CPU_stop), .Q(On_Off_Switch_q), .clk(controlled_buffer_1_out));  // open: en, clr
  EXT_Numpad2Bin Keypad_Encoder (.in_1({_9, _8, _7, _6, _5, _4, _3, _2, _1, _0}), .out_2(Keypad_Encoder_out_2));
  Register #(.trigger("high")) Buffer (.D(Keypad_Encoder_out_2), .Q(Buffer_q), .clk(1'b1));  // open: en, clr
  CPU CPU (
    .A_OUT(CPU_a_out), .RW(CPU_rw), .D_IN(ram_1_data), .Keypad_Input(Buffer_q),
    .Display_Out(CPU_display_out), .stop(CPU_stop), .CLOCK(controlled_buffer_1_out), .D_OUT(CPU_d_out));
  Register buffer_2 (.D(CPU_display_out), .Q(buffer_2_q), .clk(controlled_buffer_1_out));  // open: en, clr
  D_Flip_Flop RW (.clk(controlled_buffer_1_out), .D(CPU_rw), .Q(RW_q));  // open: Qn, preset, en, reset
  EXT_DisplayDriver ext_displaydriver_1 (
    .x3(buffer_2_q[7]), .x2(buffer_2_q[6]), .x1(buffer_2_q[5]), .x0(buffer_2_q[4]),
    .e0(ext_displaydriver_1_e0), .e1(ext_displaydriver_1_e1), .e2(ext_displaydriver_1_e2),
    .e3(ext_displaydriver_1_e3), .e4(ext_displaydriver_1_e4), .e5(ext_displaydriver_1_e5),
    .e6(ext_displaydriver_1_e6));
  EXT_DisplayDriver ext_displaydriver_2 (
    .x3(buffer_2_q[3]), .x2(buffer_2_q[2]), .x1(buffer_2_q[1]), .x0(buffer_2_q[0]),
    .e0(ext_displaydriver_2_e0), .e1(ext_displaydriver_2_e1), .e2(ext_displaydriver_2_e2),
    .e3(ext_displaydriver_2_e3), .e4(ext_displaydriver_2_e4), .e5(ext_displaydriver_2_e5),
    .e6(ext_displaydriver_2_e6));
  _7_Segment_Display u_7_segment_display_1 (
    .g(ext_displaydriver_1_e6), .f(ext_displaydriver_1_e5), .a(ext_displaydriver_1_e0),
    .b(ext_displaydriver_1_e1), .e(ext_displaydriver_1_e4), .d(ext_displaydriver_1_e3),
    .c(ext_displaydriver_1_e2));  // open: dp
  RAM #(.bus("separate")) ram_1 (
    .addr(CPU_a_out), .din(CPU_d_out), .data(ram_1_data), .str(RW_q), .clk(controlled_buffer_1_out));  // open: sel, ld, clr
  _7_Segment_Display u_7_segment_display_2 (
    .g(ext_displaydriver_2_e6), .f(ext_displaydriver_2_e5), .a(ext_displaydriver_2_e0),
    .b(ext_displaydriver_2_e1), .e(ext_displaydriver_2_e4), .d(ext_displaydriver_2_e3),
    .c(ext_displaydriver_2_e2));  // open: dp

  // Notes on the sheet:
  //   <- On Off Switch. set 0 to enable system
  //   RAM
endmodule

module ALU_Module (
  input  [7:0] L,
  input  [7:0] R,
  input  [1:0] ALUOP,
  output [7:0] out_4,
  output Zero,
  output Negative,
  output OverFlow
);

  wire not_1_out, not_2_out, not_3_out, not_4_out, not_5_out, not_6_out, not_7_out;
  wire [7:0] adder_1_out, xor_1_out;

  Adder adder_1 (.a(L), .b(R), .out(adder_1_out), .cout(OverFlow));  // open: cin
  assign xor_1_out = L ^ R;  // XOR_Gate xor_1, 8 bits wide
  Multiplexer #(.select(2), .width(8), .enable("false")) multiplexer_1 (
    .in0(adder_1_out), .in1(xor_1_out), .in2(adder_1_out), .in3(adder_1_out), .out(out_4), .sel(ALUOP));
  not not_1 (not_1_out, out_4[0]);
  not not_2 (not_2_out, out_4[1]);
  not not_3 (not_3_out, out_4[2]);
  not not_4 (not_4_out, out_4[3]);
  not not_5 (not_5_out, out_4[4]);
  not not_6 (not_6_out, out_4[5]);
  not not_7 (not_7_out, out_4[6]);
  not not_8 (Negative, out_4[7]);
  and and_1 (Zero, not_1_out, not_2_out, not_3_out, not_4_out, not_5_out, not_6_out, not_7_out, Negative);
endmodule

module EXT_Numpad2Bin (
  input  [9:0] in_1,
  output [7:0] out_2
);

  wire [7:0] bit_extender_1_out, bit_extender_2_out, bit_extender_3_out, bit_extender_4_out,
       bit_extender_5_out, bit_extender_6_out, bit_extender_7_out, bit_extender_8_out, bit_extender_9_out,
       bit_extender_10_out, not_1_out, not_16_out, not_29_out, not_42_out, not_53_out;
  wire [7:1] not_9_out, not_36_out, not_60_out;
  wire [7:2] not_23_out;
  wire [7:3] not_48_out;

  not not_1 (not_1_out[0], bit_extender_1_out[0]);
  not not_2 (not_1_out[1], bit_extender_1_out[1]);
  not not_3 (not_1_out[2], bit_extender_1_out[2]);
  not not_4 (not_1_out[3], bit_extender_1_out[3]);
  not not_5 (not_1_out[4], bit_extender_1_out[4]);
  assign bit_extender_1_out = {{7{in_1[0]}}, in_1[0]};  // Bit_Extender bit_extender_1
  not not_6 (not_1_out[5], bit_extender_1_out[5]);
  not not_7 (not_1_out[6], bit_extender_1_out[6]);
  not not_8 (not_1_out[7], bit_extender_1_out[7]);
  not not_9 (not_9_out[1], bit_extender_2_out[1]);
  not not_10 (not_9_out[2], bit_extender_2_out[2]);
  not not_11 (not_9_out[3], bit_extender_2_out[3]);
  not not_12 (not_9_out[4], bit_extender_2_out[4]);
  assign bit_extender_2_out = {{7{in_1[1]}}, in_1[1]};  // Bit_Extender bit_extender_2
  not not_13 (not_9_out[5], bit_extender_2_out[5]);
  not not_14 (not_9_out[6], bit_extender_2_out[6]);
  not not_15 (not_9_out[7], bit_extender_2_out[7]);
  not not_16 (not_16_out[0], bit_extender_3_out[0]);
  not not_17 (not_16_out[2], bit_extender_3_out[2]);
  not not_18 (not_16_out[3], bit_extender_3_out[3]);
  not not_19 (not_16_out[4], bit_extender_3_out[4]);
  assign bit_extender_3_out = {{7{in_1[2]}}, in_1[2]};  // Bit_Extender bit_extender_3
  not not_20 (not_16_out[5], bit_extender_3_out[5]);
  not not_21 (not_16_out[6], bit_extender_3_out[6]);
  not not_22 (not_16_out[7], bit_extender_3_out[7]);
  not not_23 (not_23_out[2], bit_extender_4_out[2]);
  not not_24 (not_23_out[3], bit_extender_4_out[3]);
  not not_25 (not_23_out[4], bit_extender_4_out[4]);
  assign bit_extender_4_out = {{7{in_1[3]}}, in_1[3]};  // Bit_Extender bit_extender_4
  not not_26 (not_23_out[5], bit_extender_4_out[5]);
  not not_27 (not_23_out[6], bit_extender_4_out[6]);
  not not_28 (not_23_out[7], bit_extender_4_out[7]);
  not not_29 (not_29_out[0], bit_extender_5_out[0]);
  not not_30 (not_29_out[1], bit_extender_5_out[1]);
  not not_31 (not_29_out[3], bit_extender_5_out[3]);
  not not_32 (not_29_out[4], bit_extender_5_out[4]);
  assign bit_extender_5_out = {{7{in_1[4]}}, in_1[4]};  // Bit_Extender bit_extender_5
  not not_33 (not_29_out[5], bit_extender_5_out[5]);
  not not_34 (not_29_out[6], bit_extender_5_out[6]);
  not not_35 (not_29_out[7], bit_extender_5_out[7]);
  not not_36 (not_36_out[1], bit_extender_6_out[1]);
  not not_37 (not_36_out[3], bit_extender_6_out[3]);
  not not_38 (not_36_out[4], bit_extender_6_out[4]);
  assign bit_extender_6_out = {{7{in_1[5]}}, in_1[5]};  // Bit_Extender bit_extender_6
  not not_39 (not_36_out[5], bit_extender_6_out[5]);
  not not_40 (not_36_out[6], bit_extender_6_out[6]);
  not not_41 (not_36_out[7], bit_extender_6_out[7]);
  not not_42 (not_42_out[0], bit_extender_7_out[0]);
  not not_43 (not_42_out[3], bit_extender_7_out[3]);
  not not_44 (not_42_out[4], bit_extender_7_out[4]);
  assign bit_extender_7_out = {{7{in_1[6]}}, in_1[6]};  // Bit_Extender bit_extender_7
  not not_45 (not_42_out[5], bit_extender_7_out[5]);
  not not_46 (not_42_out[6], bit_extender_7_out[6]);
  not not_47 (not_42_out[7], bit_extender_7_out[7]);
  not not_48 (not_48_out[3], bit_extender_8_out[3]);
  not not_49 (not_48_out[4], bit_extender_8_out[4]);
  assign bit_extender_8_out = {{7{in_1[7]}}, in_1[7]};  // Bit_Extender bit_extender_8
  not not_50 (not_48_out[5], bit_extender_8_out[5]);
  not not_51 (not_48_out[6], bit_extender_8_out[6]);
  not not_52 (not_48_out[7], bit_extender_8_out[7]);
  not not_53 (not_53_out[0], bit_extender_9_out[0]);
  not not_54 (not_53_out[1], bit_extender_9_out[1]);
  not not_55 (not_53_out[2], bit_extender_9_out[2]);
  not not_56 (not_53_out[4], bit_extender_9_out[4]);
  assign bit_extender_9_out = {{7{in_1[8]}}, in_1[8]};  // Bit_Extender bit_extender_9
  not not_57 (not_53_out[5], bit_extender_9_out[5]);
  not not_58 (not_53_out[6], bit_extender_9_out[6]);
  not not_59 (not_53_out[7], bit_extender_9_out[7]);
  not not_60 (not_60_out[1], bit_extender_10_out[1]);
  not not_61 (not_60_out[2], bit_extender_10_out[2]);
  assign bit_extender_10_out = {{7{in_1[9]}}, in_1[9]};  // Bit_Extender bit_extender_10
  not not_62 (not_60_out[4], bit_extender_10_out[4]);
  not not_63 (not_60_out[5], bit_extender_10_out[5]);
  not not_64 (not_60_out[6], bit_extender_10_out[6]);
  not not_65 (not_60_out[7], bit_extender_10_out[7]);
  assign out_2 = in_1[0] ? not_1_out : 8'bz;  // Controlled_Buffer controlled_buffer_1
  assign out_2 = in_1[1] ? {not_9_out, bit_extender_2_out[0]} : 8'bz;  // Controlled_Buffer controlled_buffer_2
  assign out_2 = in_1[2] ? {not_16_out[7:2], bit_extender_3_out[1], not_16_out[0]} : 8'bz;  // Controlled_Buffer controlled_buffer_3
  assign out_2 = in_1[3] ? {not_23_out, bit_extender_4_out[1:0]} : 8'bz;  // Controlled_Buffer controlled_buffer_4
  assign out_2 = in_1[4] ? {not_29_out[7:3], bit_extender_5_out[2], not_29_out[1:0]} : 8'bz;  // Controlled_Buffer controlled_buffer_5
  assign out_2 = in_1[5] ? {not_36_out[7:3], bit_extender_6_out[2], not_36_out[1], bit_extender_6_out[0]} : 8'bz;  // Controlled_Buffer controlled_buffer_6
  assign out_2 = in_1[6] ? {not_42_out[7:3], bit_extender_7_out[2:1], not_42_out[0]} : 8'bz;  // Controlled_Buffer controlled_buffer_7
  assign out_2 = in_1[7] ? {not_48_out, bit_extender_8_out[2:0]} : 8'bz;  // Controlled_Buffer controlled_buffer_8
  assign out_2 = in_1[8] ? {not_53_out[7:4], bit_extender_9_out[3], not_53_out[2:0]} : 8'bz;  // Controlled_Buffer controlled_buffer_9
  assign out_2 = in_1[9] ? {not_60_out[7:4], bit_extender_10_out[3], not_60_out[2:1], bit_extender_10_out[0]} : 8'bz;  // Controlled_Buffer controlled_buffer_10
endmodule

module EXT_DisplayDriver (
  input  x3,
  input  x2,
  input  x1,
  input  x0,
  output e0,
  output e1,
  output e2,
  output e3,
  output e4,
  output e5,
  output e6
);

  wire _0000_out, _0010_2_out, _0010_out, _0011_out, _0100_2_out, _0100_out, _0101_2_out, _0101_out,
       _0110_out, _0111_out, _1000_out, _1001_out, _1010_2_out, _1010_out, _1011_out, _1100_2_out, _1100_out,
       _1101_2_out, _1101_out, _1110_out, _1111_out, and_1_out, and_2_out, nand_2_out, not_1_out, not_2_out,
       not_3_out, not_4_out, not_5_out, not_6_out, not_7_out, not_8_out, not_9_out, not_10_out, not_11_out,
       not_12_out, not_13_out, not_14_out, not_15_out, not_16_out, not_17_out, not_18_out, not_19_out,
       not_20_out, not_21_out, not_22_out, not_23_out, not_24_out, not_25_out, not_26_out, not_27_out,
       not_28_out, not_29_out, not_30_out, not_31_out, not_32_out, not_33_out, not_34_out, not_35_out,
       not_36_out, not_37_out, not_38_out, not_39_out, not_40_out, not_41_out, not_42_out, not_43_out,
       not_44_out, or_2_out, or_3_out, or_4_out, or_5_out, or_6_out, or_7_out, or_8_out, or_9_out, OR_out;

  not not_1 (not_1_out, x3);
  not not_2 (not_2_out, x2);
  not not_3 (not_3_out, x1);
  not not_4 (not_4_out, x3);
  not not_5 (not_5_out, x1);
  not not_6 (not_6_out, x0);
  not not_7 (not_7_out, x2);
  not not_8 (not_8_out, x1);
  not not_9 (not_9_out, x3);
  not not_10 (not_10_out, x1);
  not not_11 (not_11_out, x3);
  not not_12 (not_12_out, x0);
  not not_13 (not_13_out, x1);
  not not_14 (not_14_out, x0);
  not not_15 (not_15_out, x0);
  not not_16 (not_16_out, x3);
  not not_17 (not_17_out, x1);
  not not_18 (not_18_out, x0);
  not not_19 (not_19_out, x3);
  not not_20 (not_20_out, x2);
  not not_21 (not_21_out, x0);
  not not_22 (not_22_out, x3);
  not not_23 (not_23_out, x2);
  not not_24 (not_24_out, x3);
  not not_25 (not_25_out, x1);
  not not_26 (not_26_out, x0);
  not not_27 (not_27_out, x3);
  not not_28 (not_28_out, x1);
  not not_29 (not_29_out, x2);
  not not_30 (not_30_out, x1);
  not not_31 (not_31_out, x3);
  not not_32 (not_32_out, x2);
  not not_33 (not_33_out, x0);
  not not_34 (not_34_out, x1);
  not not_35 (not_35_out, x2);
  not not_36 (not_36_out, x0);
  not not_37 (not_37_out, x1);
  not not_38 (not_38_out, x0);
  not not_39 (not_39_out, x3);
  not not_40 (not_40_out, x2);
  not not_41 (not_41_out, x0);
  and and_1 (and_1_out, not_1_out, not_2_out, not_3_out, x0);
  and and_2 (and_2_out, not_4_out, x2, not_5_out, not_6_out);
  and _1011 (_1011_out, x3, not_7_out, x1, x0);
  and _1101 (_1101_out, x3, x2, not_8_out, x0);
  and _0101 (_0101_out, not_9_out, x2, not_10_out, x0);
  and _0110 (_0110_out, not_11_out, x2, x1, not_12_out);
  and _1100 (_1100_out, x3, x2, not_13_out, not_14_out);
  and _1110 (_1110_out, x3, x2, x1, not_15_out);
  and _1111 (_1111_out, x3, x2, x1, x0);
  and _0010 (_0010_out, not_39_out, not_40_out, x1, not_41_out);
  and _0100 (_0100_out, not_16_out, x2, not_17_out, not_18_out);
  and _0111 (_0111_out, not_19_out, x2, x1, x0);
  and _1010 (_1010_out, x3, not_20_out, x1, not_21_out);
  and _0011 (_0011_out, not_22_out, not_23_out, x1, x0);
  and _0100_2 (_0100_2_out, not_24_out, x2, not_25_out, not_26_out);
  and _0101_2 (_0101_2_out, not_27_out, x2, not_28_out, x0);
  and _1001 (_1001_out, x3, not_29_out, not_30_out, x0);
  and _0010_2 (_0010_2_out, not_31_out, not_32_out, x1, not_33_out);
  and _1101_2 (_1101_2_out, x3, x2, not_34_out, x0);
  and _1010_2 (_1010_2_out, x3, not_35_out, x1, not_36_out);
  and _1100_2 (_1100_2_out, x3, x3, not_37_out, not_38_out);
  and _0000 (_0000_out, ~x3, ~x2, ~x1, ~x0);  // AND_Gate
  or OR (OR_out, x3, x2, x1, x0);
  or or_2 (or_2_out, and_1_out, _1010_2_out, _1100_2_out, _0000_out, _0111_out);
  or or_3 (or_3_out, and_1_out, and_2_out, _1011_out, _1101_out);
  or or_4 (or_4_out, and_1_out, _1011_out, _0101_out, _0110_out, _1100_out, _1110_out, _1111_out);
  or or_5 (or_5_out, and_1_out, _1100_out, _1110_out, _1111_out, _0010_out);
  or or_6 (or_6_out, and_1_out, _1111_out, _0100_out, _0111_out, _1010_out);
  or or_7 (or_7_out, _0011_out, _0100_2_out, _0101_2_out, _1001_out, _0111_out);
  or or_8 (or_8_out, _0011_out, _0010_2_out, _1101_2_out, _0111_out);
  or or_9 (or_9_out, _0000_out, OR_out);
  nand nand_1 (e5, OR_out, or_8_out);
  nand nand_2 (nand_2_out, or_2_out, or_9_out);
  not not_42 (not_42_out, x2);
  not not_43 (not_43_out, x1);
  not not_44 (not_44_out, x0);
  nand nand_3 (e0, or_3_out, OR_out);
  nand nand_4 (e1, OR_out, or_4_out);
  nand nand_5 (e2, OR_out, or_5_out);
  nand nand_6 (e3, OR_out, or_6_out);
  nand nand_7 (e4, OR_out, or_7_out);
  and _1000 (_1000_out, x3, not_42_out, not_43_out, not_44_out);
  or or_10 (e6, nand_2_out, _1000_out);

  // Notes on the sheet:
  //   0001
  //   0100
  //   1111
  //   1111
  //   1011
  //   1100
  //   1110
  //   0111
  //   0011
  //   0111
  //   0001
  //   0001
  //   0001
  //   0001
  //   0111
  //   0001
  //   bar 0
  //   bar 1
  //   bar 2
  //   bar 3
  //   bar 4
  //   bar 5
  //   bar 6
endmodule

module CPU_Registers (
  input  Clock,
  input  [7:0] Input_Value,
  input  Register_Selector,
  input  RW,
  input  lselect,
  input  rselect,
  output [7:0] output_value,
  output [7:0] dbus,
  output [7:0] sbus,
  output [7:0] r0,
  output [7:0] r1
);

  wire demultiplexer_2_out0, demultiplexer_2_out1;
  wire [7:0] demultiplexer_1_out0, demultiplexer_1_out1;

  Demultiplexer #(.width(8)) demultiplexer_1 (
    .out0(demultiplexer_1_out0), .out1(demultiplexer_1_out1), .in(Input_Value), .sel(Register_Selector));  // open: en
  Demultiplexer demultiplexer_2 (
    .out0(demultiplexer_2_out0), .out1(demultiplexer_2_out1), .in(RW), .sel(Register_Selector));  // open: en
  Register #(.trigger("falling")) u_r0 (
    .D(demultiplexer_1_out0), .en(demultiplexer_2_out0), .Q(r0), .clk(Clock));  // open: clr
  Register #(.trigger("falling")) u_r1 (
    .D(demultiplexer_1_out1), .en(demultiplexer_2_out1), .Q(r1), .clk(Clock));  // open: clr
  Multiplexer #(.width(8), .enable("false")) multiplexer_1 (
    .in0(r0), .in1(r1), .out(output_value), .sel(Register_Selector));
  Multiplexer #(.width(8), .enable("false")) multiplexer_2 (.in0(r0), .in1(r1), .out(dbus), .sel(lselect));
  Multiplexer #(.width(8), .enable("false")) multiplexer_3 (.in0(r0), .in1(r1), .out(sbus), .sel(rselect));
endmodule

module CPU (
  input  CLOCK,
  input  [7:0] D_IN,
  input  [7:0] Keypad_Input,
  output [7:0] A_OUT,
  output RW,
  output [7:0] Display_Out,
  output [7:0] D_OUT,
  output stop
);

  wire alu_module_1_negative, alu_module_1_zero, arload, displayout, dregsel, dwrite, irload, keypadin,
       pcload, pcsel, sregsel;
  wire [1:0] addrsel, aluop, regsel;
  wire [7:0] adder_1_out, alu_module_1_out_4, multiplexer_1_out, multiplexer_2_out, multiplexer_3_out,
       multiplexer_4_out, register_1_q, register_2_q, register_3_q, sbus;

  Register #(.trigger("falling")) MAR (.D(multiplexer_1_out), .Q(A_OUT), .clk(CLOCK));  // open: en, clr
  Multiplexer #(.select(2), .width(8), .enable("false")) multiplexer_1 (
    .in0(register_3_q), .in1(register_2_q), .in2(sbus), .in3(D_OUT), .out(multiplexer_1_out), .sel(addrsel));
  Multiplexer #(.width(8), .enable("false")) multiplexer_2 (
    .in0(D_IN), .in1(Keypad_Input), .out(multiplexer_2_out), .sel(keypadin));
  Register register_1 (.D(D_IN), .en(irload), .Q(register_1_q), .clk(CLOCK));  // open: clr
  Register register_2 (.D(multiplexer_2_out), .en(arload), .Q(register_2_q), .clk(CLOCK));  // open: clr
  CU cu_1 (
    .CLOCK(CLOCK), .zero(alu_module_1_zero), .irvalue(register_1_q), .dregsel(dregsel), .sregsel(sregsel),
    .aluop(aluop), .irload(irload), .imload(arload), .pcsel(pcsel), .readwrite(RW), .pcload(pcload),
    .regsel(regsel), .dwrite(dwrite), .addrsel(addrsel), .DisplayOUT(displayout), .keypad_in(keypadin),
    .STOP_signal(stop));  // open: phase
  Multiplexer #(.select(2), .width(8), .enable("false")) multiplexer_3 (
    .in0(register_2_q), .in1(sbus), .in2(D_IN), .in3(alu_module_1_out_4), .out(multiplexer_3_out),
    .sel(regsel));
  Multiplexer #(.width(8), .enable("false")) multiplexer_4 (
    .in0(register_2_q), .in1(adder_1_out), .out(multiplexer_4_out), .sel(pcsel));
  Register register_3 (.D(multiplexer_4_out), .en(pcload), .Q(register_3_q), .clk(CLOCK));  // open: clr
  CPU_Registers cpu_registers_1 (
    .Input_Value(multiplexer_3_out), .Register_Selector(dregsel), .Clock(CLOCK), .RW(dwrite),
    .lselect(dregsel), .rselect(sregsel), .dbus(D_OUT), .sbus(sbus));  // open: output_value, r0, r1
  Adder adder_1 (.a(register_3_q), .b(8'h1), .out(adder_1_out));  // open: cin, cout
  assign Display_Out = displayout ? D_OUT : 8'bz;  // Controlled_Buffer controlled_buffer_1
  ALU_Module alu_module_1 (
    .L(D_OUT), .R(sbus), .Zero(alu_module_1_zero), .Negative(alu_module_1_negative), .ALUOP(aluop),
    .out_4(alu_module_1_out_4));  // open: OverFlow

  // Other names for the same wires on the sheet: dbus[7:0] = D_OUT; readwrite = RW

  // Notes on the sheet:
  //   IR
  //   CU
  //   Argument Register
  //   PC
  //   PC Adder
  //   Regs
  //   Wordlist
  //   sel -> selector
  //   reg -> register
  //   s -> source
  //   d -> destination
  //   ar -> argument
  //   regsel -> register selector (you guessed it)
  //   ALU
endmodule

module CU (
  input  [7:0] irvalue,
  input  CLOCK,
  input  zero,
  output [1:0] phase,
  output dregsel,
  output sregsel,
  output [1:0] aluop,
  output irload,
  output imload,
  output pcsel,
  output readwrite,
  output pcload,
  output [1:0] regsel,
  output dwrite,
  output [1:0] addrsel,
  output DisplayOUT,
  output keypad_in,
  output STOP_signal
);

  wire and_1_out, and_2_out, and_3_out, and_4_out, and_5_out, and_6_out, multiplexer_2_out,
       multiplexer_8_out, not_1_out, or_1_out;
  wire [1:0] multiplexer_3_out, multiplexer_13_out;

  and and_1 (and_1_out, ~irvalue[4], ~irvalue[5], irvalue[6], ~irvalue[7]);  // AND_Gate
  Multiplexer #(.select(2), .enable("false")) multiplexer_1 (
    .in0(1'b1), .in1(1'b0), .in2(1'b0), .in3(1'b0), .out(irload), .sel(phase));
  not not_1 (not_1_out, irvalue[6]);
  Multiplexer #(.select(2), .enable("false")) multiplexer_2 (
    .in0(1'b0), .in1(zero), .in2(1'b0), .in3(1'b0), .out(multiplexer_2_out), .sel(irvalue[5:4]));
  Multiplexer #(.select(4), .width(2), .enable("false")) multiplexer_3 (
    .in0(2'b11), .in1(2'b11), .in2(2'b11), .in3(2'b11), .in4(2'b00), .in5(2'b00), .in6(2'b01), .in7(2'b00),
    .in8(2'b00), .in9(2'b00), .in10(2'b00), .in11(2'b00), .in12(2'b10), .in13(2'b00), .in14(2'b00),
    .in15(2'b00), .out(multiplexer_3_out), .sel(irvalue[7:4]));
  and and_2 (and_2_out, not_1_out, irvalue[7], multiplexer_2_out);
  Multiplexer #(.select(2), .width(2), .enable("false")) multiplexer_4 (
    .in0(2'b00), .in1(2'b00), .in2(2'b00), .in3(multiplexer_3_out), .out(regsel), .sel(phase));
  Multiplexer #(.select(2), .enable("false")) multiplexer_5 (
    .in0(1'b0), .in1(and_1_out), .in2(1'b0), .in3(1'b0), .out(keypad_in), .sel(phase));
  and and_3 (and_3_out, ~irvalue[7], irvalue[6]);  // AND_Gate
  or or_1 (or_1_out, irvalue[7], and_3_out);
  Multiplexer #(.select(2), .enable("false")) multiplexer_6 (
    .in0(1'b1), .in1(irvalue[7]), .in2(and_2_out), .in3(and_2_out), .out(pcload), .sel(phase));
  Counter #(.width(2), .max('h3)) counter_1 (.Q(phase), .clk(CLOCK));  // open: load, D, count, carry, clr
  Multiplexer #(.select(2), .enable("false")) multiplexer_7 (
    .in0(1'b0), .in1(or_1_out), .in2(1'b0), .in3(1'b0), .out(imload), .sel(phase));
  Multiplexer #(.select(4), .enable("false")) multiplexer_8 (
    .in0(1'b1), .in1(1'b1), .in2(1'b1), .in3(1'b1), .in4(1'b1), .in5(1'b0), .in6(1'b1), .in7(1'b0),
    .in8(1'b0), .in9(1'b0), .in10(1'b0), .in11(1'b0), .in12(1'b1), .in13(1'b0), .in14(1'b1), .in15(1'b0),
    .out(multiplexer_8_out), .sel(irvalue[7:4]));
  and and_4 (and_4_out, irvalue[4], ~irvalue[5], irvalue[6], ~irvalue[7]);  // AND_Gate
  Multiplexer #(.select(2), .enable("false")) multiplexer_9 (
    .in0(1'b0), .in1(1'b0), .in2(1'b0), .in3(and_4_out), .out(DisplayOUT), .sel(phase));
  Multiplexer #(.select(2), .enable("false")) multiplexer_10 (
    .in0(1'b0), .in1(1'b0), .in2(1'b0), .in3(multiplexer_8_out), .out(dwrite), .sel(phase));
  Multiplexer #(.select(2), .enable("false")) multiplexer_11 (
    .in0(1'b1), .in1(1'b1), .in2(1'b0), .in3(1'b0), .out(pcsel), .sel(phase));
  and and_5 (and_5_out, irvalue[4], ~irvalue[5], irvalue[6], irvalue[7]);  // AND_Gate
  Multiplexer #(.select(2), .enable("false")) multiplexer_12 (
    .in0(1'b0), .in1(1'b0), .in2(and_5_out), .in3(1'b0), .out(readwrite), .sel(phase));
  Multiplexer #(.select(4), .width(2), .enable("false")) multiplexer_13 (
    .in0(2'b00), .in1(2'b00), .in2(2'b00), .in3(2'b00), .in4(2'b00), .in5(2'b00), .in6(2'b00), .in7(2'b00),
    .in8(2'b00), .in9(2'b00), .in10(2'b00), .in11(2'b00), .in12(2'b01), .in13(2'b01), .in14(2'b01),
    .in15(2'b00), .out(multiplexer_13_out), .sel(irvalue[7:4]));
  and and_6 (and_6_out, ~irvalue[4], irvalue[5], irvalue[6], ~irvalue[7]);  // AND_Gate
  Multiplexer #(.select(2), .enable("false")) multiplexer_14 (
    .in0(and_6_out), .in1(and_6_out), .in2(and_6_out), .in3(and_6_out), .out(STOP_signal), .sel(phase));
  Multiplexer #(.select(2), .width(2), .enable("false")) multiplexer_15 (
    .in0(2'b00), .in1(2'b00), .in2(multiplexer_13_out), .in3(multiplexer_13_out), .out(addrsel), .sel(phase));

  assign aluop = irvalue[5:4];
  assign dregsel = irvalue[3];
  assign sregsel = irvalue[2];

  // Other names for the same wires on the sheet: rs = irvalue[2]; rd = irvalue[3]; irbit4 = irvalue[4];
  //   op1op2[3:0] = irvalue[7:4]; op2[1:0] = irvalue[5:4]; irbit5 = irvalue[5]; irbit6 = irvalue[6];
  //   op1[1:0] = irvalue[7:6]; irbit7 = irvalue[7]; stop = STOP_signal

  // Notes on the sheet:
  //   IR Load
  //   PC Load
  //   Register Select
  //   regselector out
  //   CU
  //   Argument
  //   phase counting
  //   Read/Write
  //   Dest Reg Write
  //   PC Select
  //   setup shorthand
  //   Address Select
endmodule
