// Logisim project parte1.circ as structural Verilog: 1 circuit, main circuit main
module main (
  input  in_1,
  input  in_2,
  input  in_3,
  input  in_4,
  input  in_5,
  output out_6,
  output out_7,
  output out_8
);

  wire and_1_out, not_1_out, or_1_out;

  and and_1 (and_1_out, in_1, in_1, in_2, in_2);
  or or_1 (or_1_out, and_1_out, and_1_out, in_3, in_3);
  not not_1 (not_1_out, in_4);
  Multiplexer #(.enable("false")) multiplexer_1 (.in0(or_1_out), .in1(not_1_out), .out(out_6), .sel(in_5));
  Demultiplexer #(.enable("false")) demultiplexer_1 (.out0(out_7), .out1(out_8), .in(out_6), .sel(in_5));
endmodule
