// Logisim project parte2.circ as structural Verilog: 1 circuit, main circuit main
module main (
  input  [3:0] in_1,
  input  [3:0] in_2,
  input  [3:0] in_3,
  input  [3:0] in_4,
  output [3:0] out_5,
  output [3:0] out_6,
  output [3:0] out_7
);

  Adder #(.width(4)) adder_1 (.a(in_2), .b(in_3), .out(out_6));  // open: cin, cout
  Subtractor #(.width(4)) subtractor_1 (.a(in_1), .b(out_6), .out(out_5));  // open: bin, bout
  Adder #(.width(4)) adder_2 (.a(out_6), .b(in_4), .out(out_7));  // open: cin, cout
endmodule
