// Logisim project parte3.circ as structural Verilog: 1 circuit, main circuit main
module main (
  input  [3:0] in_1,
  input  [3:0] in_2,
  input  in_3,
  output [3:0] out_4
);

  wire clock_1_out;
  wire [3:0] adder_1_out, multiplexer_1_out;

  Multiplexer #(.width(4), .enable("false")) multiplexer_1 (
    .in0(adder_1_out), .in1(in_1), .out(multiplexer_1_out), .sel(in_3));
  Register #(.width(4)) register_1 (.D(multiplexer_1_out), .Q(out_4), .clk(clock_1_out));  // open: en, clr
  Clock clock_1 (.out(clock_1_out));
  Adder #(.width(4)) adder_1 (.a(out_4), .b(in_2), .out(adder_1_out));  // open: cin, cout
  // Probe on out_4
endmodule
