// Logisim project parte4.circ as structural Verilog: 1 circuit, main circuit main
module main (
  input  [3:0] in_1,
  input  in_2,
  input  Enable,
  input  Seletor,
  input  load_IR
);

  wire clock_1_out, clock_2_out;
  wire [3:0] multiplexer_1_out, ram_1_data, register_1_q, rom_1_data;

  Clock clock_1 (.out(clock_1_out));
  RAM #(.addrWidth(4), .dataWidth(4)) ram_1 (
    .addr(in_1), .data(ram_1_data), .sel(Enable), .clk(clock_1_out), .ld(in_2));  // open: clr
  ROM #(.addrWidth(4), .dataWidth(4)) rom_1 (.addr(in_1), .data(rom_1_data), .sel(Enable));
  Multiplexer #(.width(4), .enable("false")) multiplexer_1 (
    .in0(ram_1_data), .in1(rom_1_data), .out(multiplexer_1_out), .sel(Seletor));
  Clock clock_2 (.out(clock_2_out));
  // Probe on register_1_q
  // Probe on register_1_q
  Register #(.width(4)) register_1 (
    .D(multiplexer_1_out), .en(load_IR), .Q(register_1_q), .clk(clock_2_out));  // open: clr

  // Notes on the sheet:
  //   Memoria RAM
  //   Memoria ROM
endmodule
